# Fritzing sketch Laser Viscometer (saved by Fritzing 0.9.3b)
breadboards: 1

parts:
  Part1 = Arduino Nano (Rev3.0)
  Laser_Switch = Pushbutton [package="[THT]"]
  Laser1 = KY-008 Laser Transmitter Module [package="Breakout board"]
  Laser2 = KY-008 Laser Transmitter Module [package="Breakout board"]
  Photocell1 = Photocell (LDR) [package=THT]
  Photocell2 = Photocell (LDR) [package=THT]
  J1 = Piezo Speaker
  R1 = Resistor [tolerance=±5% resistance=220 package=THT]

nets:
  N1: Part1.GND, Laser1.-, Laser2.-, J1.pin1, R1.Pin_1
  N2: Part1.D2, Photocell1.pin_0
  N3: Part1.D3, Photocell2.pin_0
  N4: Part1.D4, Laser_Switch.Pin_3, Laser_Switch.Pin_4, R1.Pin_0
  N5: Part1.D5, J1.pin2
  N6: Part1.5V, Laser_Switch.Pin_1, Laser_Switch.Pin_2, Photocell1.pin_1, Photocell2.pin_1
  N7: Part1.D13/SCK, Laser1.S, Laser2.S

custom parts:
  KY-008 Laser Transmitter Module: Laser Transmitter module KY-008 for Arduino, emits a dot shaped red laser beam.
